# Fritzing sketch Diagrama de Circuitos (saved by Fritzing 0.9.3b)
breadboards: 1

parts:
  U1 = NodeMCU V3.0
  J1 = Basic Servo
  J2 = Piezo Speaker

nets:
  N1: U1.GND#6, U1.GND#13, U1.GND#16, U1.GND#33, J1.gnd, J2.pin1
  N2: U1.D5, J2.pin2
  N3: U1.D7, J1.pulse
  VIN: U1.Vin, J1.vcc

custom parts:
  NodeMCU V3.0: ESP8266 based NodeMCU
