# Fritzing sketch MQ135BuzzerFan (saved by Fritzing 0.9.3b)
breadboards: 1

parts:
  U1 = NodeMCU V3.0
  J1 = Piezo Speaker
  F1 = Fan - Ventilador [package=THT]
  Part2 = MQ-7 breakout

nets:
  N1: U1.D1, Part2.DO
  N2: U1.D2, F1.5V
  N3: U1.D3, J1.pin2
  GND: U1.GND#6, U1.GND#13, U1.GND#16, U1.GND#33, J1.pin1, F1.GND, Part2.GND
  VIN: U1.Vin, Part2.VCC

custom parts:
  NodeMCU V3.0: ESP8266 based NodeMCU
  Fan - Ventilador: Ventilador de 2 pines, se encuentra comunmente en computadoras de escritorio
  MQ-7 breakout: SKU: 101282
